// Logisim project BasicComp.circ as structural Verilog: 2 circuits, main circuit Project
module main (
  input  [15:0] in_1,
  input  [15:0] in_2,
  input  [2:0] Selection_Lines,
  output [15:0] out_4
);

  wire [15:0] adder_1_out, adder_2_out, and_1_out, or_1_out, subtractor_1_out, xor_1_out;

  Subtractor #(.width(16)) subtractor_1 (.a(in_1), .b(in_2), .out(subtractor_1_out));  // open: bin, bout
  Adder #(.width(16)) adder_1 (.a(in_1), .b(in_2), .out(adder_1_out));  // open: cin, cout
  assign and_1_out = in_1 & in_2;  // AND_Gate and_1, 16 bits wide
  assign or_1_out = in_1 | in_2;  // OR_Gate or_1, 16 bits wide
  assign xor_1_out = in_1 ^ in_2;  // XOR_Gate xor_1, 16 bits wide
  Adder #(.width(16)) adder_2 (.a(in_1), .b(16'h1), .out(adder_2_out));  // open: cin, cout
  Multiplexer #(.select(3), .width(16), .enable("false")) multiplexer_1 (
    .in1(adder_1_out), .in2(subtractor_1_out), .in3(in_1), .in4(and_1_out), .in5(or_1_out), .in6(xor_1_out),
    .in7(adder_2_out), .out(out_4), .sel(Selection_Lines));  // open: in0
endmodule

module Project (
  input  in_1,
  input  in_2,
  input  in_3,
  input  in_4,
  input  in_5,
  input  in_6,
  input  [2:0] in_7,
  input  [2:0] in_8,
  input  in_9
);

  wire clock_1_out;
  wire [6:0] AR_q, bit_extender_1_out;
  wire [15:0] AC_q, ALU_out_4, bit_extender_2_out, DR_q, multiplexer_1_out, ram_1_data, TR_q;

  Bit_Extender #(.in_width(16), .out_width(7)) bit_extender_1 (.in(multiplexer_1_out), .out(bit_extender_1_out));
  Register #(.width(7)) AR (.D(bit_extender_1_out), .en(in_4), .Q(AR_q), .clk(clock_1_out));  // open: clr
  Register #(.width(16)) TR (.D(multiplexer_1_out), .en(in_5), .Q(TR_q), .clk(clock_1_out));  // open: clr
  Register #(.width(16)) DR (.D(multiplexer_1_out), .en(in_6), .Q(DR_q), .clk(clock_1_out));  // open: clr
  main ALU (.in_1(DR_q), .in_2(AC_q), .Selection_Lines(in_8), .out_4(ALU_out_4));
  assign bit_extender_2_out = {{9{1'b0}}, AR_q};  // Bit_Extender bit_extender_2
  Register #(.width(16)) AC (.D(ALU_out_4), .en(in_9), .Q(AC_q), .clk(clock_1_out));  // open: clr
  RAM #(.addrWidth(7), .dataWidth(16), .bus("separate")) ram_1 (
    .addr(AR_q), .din(multiplexer_1_out), .data(ram_1_data), .str(in_2), .sel(in_1), .clk(clock_1_out),
    .ld(in_3));  // open: clr
  Clock clock_1 (.out(clock_1_out));
  Multiplexer #(.select(3), .width(16), .enable("false")) multiplexer_1 (
    .in0(ram_1_data), .in1(bit_extender_2_out), .in2(TR_q), .in3(DR_q), .in4(AC_q), .out(multiplexer_1_out),
    .sel(in_7));  // open: in5, in6, in7
endmodule
